// Logisim project ex2.circ as structural Verilog: 1 circuit, main circuit compute_BrUn
module compute_BrUn (
  input  [31:0] INSTRUCTION,
  output BrUn
);


  assign BrUn = INSTRUCTION[13];

  // Other names for the same wires on the sheet: TUN0 = INSTRUCTION[13]
endmodule
